# Fritzing sketch generator_schematics_example (saved by Fritzing 0.8.7b)
breadboards: 1

parts:
  S1 = Pushbutton [package="[THT]"]
  S2 = Pushbutton [package="[THT]"]
  Part1 = Arduino Uno (Rev3)
  R1 = Trimmer Potentiometer [maximum_resistance=5kΩ package=THT]
  R2 = Trimmer Potentiometer [maximum_resistance=5kΩ package=THT]

nets:
  N1: S1.Pin_1, S1.Pin_2, S2.Pin_1, S2.Pin_2, Part1.GND, R1.leg1, R2.leg1
  N2: S1.Pin_3, S1.Pin_4, Part1.D2
  N3: S2.Pin_3, S2.Pin_4, Part1.D3_PWM
  N4: Part1.A1, R2.wiper
  N5: Part1.A2, R1.wiper
  N6: Part1.5V, R1.leg2, R2.leg2
